# Fritzing sketch LSM303pi2 (saved by Fritzing 0.9.3b)
circuit board: 4.10398cm x 4.19334cm

parts:
  Raspberry_Pi_1 = Raspberry Pi 3 [part_number=RPI-3-V1.2]
  J2 = female pin header, 8 pins [form="♀ (female)"]

nets:
  N1: Raspberry_Pi_1.3v3, J2.pin8
  N2: Raspberry_Pi_1.GPIO2, J2.pin3
  N3: Raspberry_Pi_1.GPIO3, J2.pin1
  N4: Raspberry_Pi_1.GND, J2.pin6

notes:
  GND
  3.3V
  SDA
  SCL
